# Fritzing sketch RocketLauncher (saved by Fritzing 0.9.3b)
circuit board: 4cm x 5cm
breadboards: 1

parts:
  Q1 = NPN-Transistor [package="TO92 [THT]"]
  Bmicro = Screw terminal - 2 pins [package=THT]
  Blaunch = Screw terminal - 2 pins [package=THT]
  LAUNCH!!! = Screw terminal - 2 pins [package=THT]
  Bmicro_2 = Battery
  RELAY = OMRON PCB Power Relay – G5LE [part_number="G5LE-1\n" package=THT]
  LED = LED - 5mm [color="Red (633nm)" package="5 mm [THT]"]
  220Ω = Resistor [tolerance=±5% resistance=220 package=THT]
  Blend_Micro = Blend Micro v1.0
  Blaunch_2 = Battery
  220Ω_2 = Resistor [tolerance=±5% resistance=220 package=THT]

nets:
  GND: Q1.E, Bmicro.pin2, Bmicro_2.-, LED.cathode, Blend_Micro.GND
  N1: Q1.B, 220Ω_2.Pin_0
  N2: Q1.C, RELAY.COIL2
  N3: Bmicro.pin1, Bmicro_2.+, RELAY.COIL1, Blend_Micro.VIN
  N4: Blaunch.pin1, RELAY.C, Blaunch_2.+
  N5: Blaunch.pin2, LAUNCH!!!.pin2, Blaunch_2.-
  N6: LAUNCH!!!.pin1, RELAY.B
  N7: LED.anode, 220Ω.Pin_0
  N8: 220Ω.Pin_1, Blend_Micro.D9/PWM/A9
  N9: Blend_Micro.D8/A8, 220Ω_2.Pin_1

notes:
  Rocket Launcher
  v1.1 2016.06.27
  github.com/Ehryk/Rockets

custom parts:
  Blend Micro v1.0: Blend Micro is a RedBearLab Arduino at Heart integrated development board, they have "blend"ed Arduino with Bluetooth 4.0 Low Energy (aka BLE or Bluetooth Smart) into a single board. It is targeted for makers to develop low power Internet-Of-Things (IoT) projects quickly and easily. The micro-controller unit (MCU) is Atmel ATmega32u4 and the BLE chip is Nordic nRF8001. Blend Micro runs as BLE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
